# Fritzing sketch layout (saved by Fritzing 0.9.9b)
breadboards: 1

parts:
  Teensy_3_1 = Teensy 3.1  # not connected
  IC1 = IC, DIP package, 16 pins [chip_label=IC]  # not connected
  R1 = Resistor [tolerance=±5% power=0.25 resistance=2.2k package=THT]  # not connected
  R2 = Resistor [tolerance=±5% power=0.25 resistance=2.2k package=THT]
  R3 = Resistor [tolerance=±5% power=0.25 resistance=2.2k package=THT]
  R4 = Resistor [tolerance=±5% power=0.25 resistance=2.2k package=THT]
  R5 = Resistor [tolerance=±5% power=0.25 resistance=3.3k package=THT]
  R6 = Resistor [tolerance=±5% power=0.25 resistance=3.3k package=THT]
  R7 = Resistor [tolerance=±5% power=0.25 resistance=3.3k package=THT]
  R8 = Resistor [tolerance=±5% power=0.25 resistance=3.3k package=THT]
  S1 = Pushbutton [package="[THT]"]
  R9 = Resistor [tolerance=±5% power=0.25 resistance=10k package=THT]
  LED1 = LED - 3mm [color="Red (633nm)" current=0.030 package="3 mm [THT]"]
  R10 = Resistor [tolerance=±5% power=0.25 resistance=10k package=THT]

nets:
  N1: R2.Pin_1, R6.Pin_0
  N2: R3.Pin_1, R8.Pin_0
  N3: R4.Pin_1, R7.Pin_0
  N4: R5.Pin_1, R6.Pin_1, R7.Pin_1, R8.Pin_1, R9.Pin_1, R10.Pin_1
  N5: S1.Pin_1, S1.Pin_2
  N6: S1.Pin_3, S1.Pin_4, R9.Pin_0
  N7: LED1.anode, R10.Pin_0
